# Fritzing sketch LittleRover (saved by Fritzing 0.9.3b)
breadboards: 1

parts:
  R1 = Resistor [tolerance=±5% resistance=330 package=THT]
  J1 = Basic Servo
  J2 = Basic Servo
  VCC1 = 4 x AAA Battery Mount
  Part1 = Arduino Nano (Rev3.0)
  hc-sr1 = hc-sr04
  LED1 = smd LED [color="Red (633nm)" package="1206 [SMD]"]
  LED2 = smd LED [color="Red (633nm)" package="1206 [SMD]"]

nets:
  GND: R1.Pin_0, J1.gnd, J2.gnd, VCC1.-, Part1.GND, hc-sr1.GND
  N1: R1.Pin_1, LED1.cathode, LED2.cathode
  VCC: J1.vcc, J2.vcc, VCC1.+, Part1.VIN, hc-sr1.VCC
  N2: J1.pulse, Part1.D5
  N3: J2.pulse, Part1.D3
  N4: Part1.D8, LED2.anode
  N5: Part1.D9, LED1.anode
  N6: Part1.A0, hc-sr1.Trig
